// Logisim project 3 x 8 using 2 x 4 Decoder.circ as structural Verilog: 2 circuits, main circuit main
module main (
  input  a,
  input  b,
  input  e,
  output out_4,
  output out_5,
  output out_6,
  output out_7,
  output out_8,
  output out_9,
  output out_10,
  output out_11
);

  wire not_1_out;

  not not_1 (not_1_out, e);
  _2_to_4 u_2_to_4_1 (.a(a), .b(b), .e(not_1_out), .d0(out_4), .d1(out_5), .d2(out_6), .d3(out_7));
  _2_to_4 u_2_to_4_2 (.a(a), .b(b), .e(e), .d0(out_8), .d1(out_9), .d2(out_10), .d3(out_11));
endmodule

module _2_to_4 (
  input  a,
  input  b,
  input  e,
  output d0,
  output d1,
  output d2,
  output d3
);

  wire not_1_out, not_2_out, not_3_out, not_4_out;

  not not_1 (not_1_out, a);
  not not_2 (not_2_out, b);
  not not_3 (not_3_out, a);
  not not_4 (not_4_out, b);
  and and_1 (d3, a, b, e);
  and and_2 (d0, not_1_out, not_2_out, e);
  and and_3 (d1, not_3_out, b, e);
  and and_4 (d2, a, not_4_out, e);
endmodule
