// Logisim project 4 x 16 using 3 x 8.circ as structural Verilog: 2 circuits, main circuit main
module main (
  input  a,
  input  b,
  input  c,
  input  E,
  output out_5,
  output out_6,
  output out_7,
  output out_8,
  output out_9,
  output out_10,
  output out_11,
  output out_12,
  output out_13,
  output out_14,
  output out_15,
  output out_16,
  output out_17,
  output out_18,
  output out_19,
  output out_20
);

  wire not_1_out;

  not not_1 (not_1_out, E);
  _3_to_8 u_3_to_8_1 (
    .a(a), .b(b), .c(b), .e(not_1_out), .d0(out_5), .d1(out_6), .d2(out_7), .d3(out_8), .d4(out_9),
    .d5(out_10), .d6(out_11), .d7(out_12));
  _3_to_8 u_3_to_8_2 (
    .a(a), .b(b), .c(b), .e(E), .d0(out_13), .d1(out_14), .d2(out_15), .d3(out_16), .d4(out_17), .d5(out_18),
    .d6(out_19), .d7(out_20));

  assign c = b;

  // Notes on the sheet:
  //   4 x 16 decoder using 3 x 8
endmodule

module _3_to_8 (
  input  a,
  input  b,
  input  c,
  input  e,
  output d0,
  output d1,
  output d2,
  output d3,
  output d4,
  output d5,
  output d6,
  output d7
);

  wire not_1_out, not_2_out, not_3_out, not_4_out, not_5_out, not_6_out, not_7_out, not_8_out, not_9_out,
       not_10_out, not_11_out, not_12_out;

  not not_1 (not_1_out, a);
  not not_2 (not_2_out, b);
  not not_3 (not_3_out, c);
  not not_4 (not_4_out, a);
  not not_5 (not_5_out, b);
  not not_6 (not_6_out, a);
  not not_7 (not_7_out, c);
  not not_8 (not_8_out, a);
  not not_9 (not_9_out, b);
  not not_10 (not_10_out, c);
  not not_11 (not_11_out, b);
  not not_12 (not_12_out, c);
  and and_1 (d7, a, b, c, e);
  and and_2 (d0, not_1_out, not_2_out, not_3_out, e);
  and and_3 (d1, not_4_out, not_5_out, c, e);
  and and_4 (d2, not_6_out, b, not_7_out, e);
  and and_5 (d3, not_8_out, b, c, e);
  and and_6 (d4, a, not_9_out, not_10_out, e);
  and and_7 (d5, a, not_11_out, c, e);
  and and_8 (d6, a, b, not_12_out, e);
endmodule
