// Logisim project Basic_gates.circ as structural Verilog: 1 circuit, main circuit main
module main (
  input  a,
  input  b,
  input  c,
  input  d,
  input  e,
  input  f,
  input  g,
  input  h,
  input  x2,
  output x,
  output y,
  output z,
  output u,
  output v
);

  not not_1 (x, a);
  and and_1 (y, b, c);
  or or_1 (z, d, e);
  nand nand_1 (u, f, g);
  nor nor_1 (v, h, x2);
endmodule
