// Logisim project D FF Reg.circ as structural Verilog: 1 circuit, main circuit main
module main (
  input  in_1,
  input  in_2,
  input  in_3,
  output out_4,
  output out_5,
  output out_6,
  output out_7,
  output out_8,
  output out_9,
  output out_10,
  output out_11,
  output out_12,
  output out_13,
  output out_14,
  output out_15,
  output out_16,
  output out_17
);

  wire button_1_out, clock_1_out, clock_2_out, clock_3_out, d_ff_1_qn, d_ff_2_qn, d_ff_3_qn, nand_1_out,
       nand_2_out, nand_5_out, nand_6_out, nand_9_out, nand_10_out, nand_13_out, nand_14_out, nand_17_out,
       nand_18_out, not_1_out, not_2_out, not_3_out, not_4_out, not_5_out;

  Clock clock_1 (.out(clock_1_out));
  not not_1 (not_1_out, in_1);
  Clock clock_2 (.out(clock_2_out));
  nand nand_1 (nand_1_out, in_1, in_1, clock_1_out);
  nand nand_2 (nand_2_out, clock_1_out, not_1_out);
  not not_2 (not_2_out, in_2);
  Clock clock_3 (.out(clock_3_out));
  Button button_1 (.out(button_1_out));
  nand nand_3 (out_4, nand_1_out, out_5);
  nand nand_4 (out_5, out_4, nand_2_out);
  nand nand_5 (nand_5_out, in_2, in_2, clock_2_out);
  nand nand_6 (nand_6_out, clock_2_out, not_2_out);
  D_Flip_Flop d_ff_1 (
    .clk(clock_3_out), .D(in_3), .Q(out_14), .Qn(d_ff_1_qn), .reset(button_1_out));  // open: preset, en
  nand nand_7 (out_6, nand_5_out, out_10);
  nand nand_8 (out_10, out_6, nand_6_out);
  D_Flip_Flop d_ff_2 (
    .clk(clock_3_out), .D(d_ff_1_qn), .Q(out_15), .Qn(d_ff_2_qn), .reset(button_1_out));  // open: preset, en
  D_Flip_Flop d_ff_3 (
    .clk(clock_3_out), .D(d_ff_2_qn), .Q(out_16), .Qn(d_ff_3_qn), .reset(button_1_out));  // open: preset, en
  not not_3 (not_3_out, out_6);
  D_Flip_Flop d_ff_4 (.clk(clock_3_out), .D(d_ff_3_qn), .Q(out_17), .reset(button_1_out));  // open: Qn, preset, en
  nand nand_9 (nand_9_out, out_6, out_6, clock_2_out);
  nand nand_10 (nand_10_out, clock_2_out, not_3_out);
  nand nand_11 (out_7, nand_9_out, out_11);
  nand nand_12 (out_11, out_7, nand_10_out);
  not not_4 (not_4_out, out_7);
  nand nand_13 (nand_13_out, out_7, out_7, clock_2_out);
  nand nand_14 (nand_14_out, clock_2_out, not_4_out);
  nand nand_15 (out_8, nand_13_out, out_12);
  nand nand_16 (out_12, out_8, nand_14_out);
  not not_5 (not_5_out, out_8);
  nand nand_17 (nand_17_out, out_8, out_8, clock_2_out);
  nand nand_18 (nand_18_out, clock_2_out, not_5_out);
  nand nand_19 (out_9, nand_17_out, out_13);
  nand nand_20 (out_13, out_9, nand_18_out);
endmodule
