// Logisim project Decoder.circ as structural Verilog: 1 circuit, main circuit main
module main (
  input  a,
  input  b,
  input  c,
  output d0,
  output d1,
  output d2,
  output d3,
  output d4,
  output d5,
  output d6,
  output d7
);

  wire not_1_out, not_2_out, not_3_out, not_4_out, not_5_out, not_6_out, not_7_out, not_8_out, not_9_out,
       not_10_out, not_11_out, not_12_out;

  not not_1 (not_1_out, a);
  not not_2 (not_2_out, b);
  not not_3 (not_3_out, c);
  not not_4 (not_4_out, a);
  not not_5 (not_5_out, b);
  not not_6 (not_6_out, a);
  not not_7 (not_7_out, c);
  not not_8 (not_8_out, a);
  not not_9 (not_9_out, b);
  not not_10 (not_10_out, c);
  not not_11 (not_11_out, b);
  not not_12 (not_12_out, c);
  and and_1 (d7, a, b, c);
  and and_2 (d0, not_1_out, not_2_out, not_3_out);
  and and_3 (d1, not_4_out, not_5_out, c);
  and and_4 (d2, not_6_out, b, not_7_out);
  and and_5 (d3, not_8_out, b, c);
  and and_6 (d4, a, not_9_out, not_10_out);
  and and_7 (d5, a, not_11_out, c);
  and and_8 (d6, a, b, not_12_out);

  // Notes on the sheet:
  //   Decoder
endmodule
