// Logisim project EvenParityGenerator.circ as structural Verilog: 1 circuit, main circuit main
module main (
  input  a,
  input  b,
  input  c,
  output p
);

  ExactlyOne xor_1 (.out(p), .in0(a), .in1(b), .in2(c));

  // Notes on the sheet:
  //   Even Parity Generator
endmodule
