// Logisim project FullAdder.circ as structural Verilog
module main (
  input  A,
  input  B,
  input  C,
  output out_4,
  output out_5
);

  wire and_1_out, and_2_out, xor_1_out;

  xor xor_1 (xor_1_out, A, B);
  and and_1 (and_1_out, A, B);
  and and_2 (and_2_out, C, xor_1_out);
  xor xor_2 (out_4, xor_1_out, C);
  or or_1 (out_5, and_1_out, and_2_out);

  // Notes on the sheet:
  //   Full Adder
endmodule
