// Logisim project HalfAdder.circ as structural Verilog: 1 circuit, main circuit main
module main (
  input  A,
  input  B,
  output A___B,
  output AB
);

  xor xor_1 (A___B, A, B);
  and and_1 (AB, A, B);

  // Notes on the sheet:
  //   Half Adder
endmodule
