// Logisim project HalfSubtractor.circ as structural Verilog: 1 circuit, main circuit main
module main (
  input  A,
  input  B,
  output A___B,
  output A_prime_B
);

  wire not_1_out;

  not not_1 (not_1_out, A);
  and and_1 (A_prime_B, B, not_1_out);
  xor xor_1 (A___B, A, B);

  // Notes on the sheet:
  //   Half Subtractor
endmodule
