// Logisim project OddParityGenerator.circ as structural Verilog: 1 circuit, main circuit main
module main (
  input  A,
  input  B,
  input  C,
  output out_4
);

  wire not_1_out, xor_1_out;

  xor xor_1 (xor_1_out, B, C);
  not not_1 (not_1_out, xor_1_out);
  xor xor_2 (out_4, A, not_1_out);

  // Notes on the sheet:
  //   Odd Parity 
endmodule
