// Logisim project PIPO.circ as structural Verilog: 1 circuit, main circuit main
module main (
  input  in_1,
  input  in_2,
  input  in_3,
  input  in_4,
  input  in_5,
  input  in_6,
  input  in_7,
  input  in_8,
  input  in_9,
  input  in_10,
  input  in_11,
  input  in_12,
  output out_13,
  output out_14,
  output out_15,
  output out_16,
  output out_17,
  output out_18,
  output out_19,
  output out_20,
  output out_21,
  output out_22,
  output out_23,
  output out_24
);

  wire button_1_out, button_2_out, button_3_out, clock_1_out, clock_2_out, clock_3_out, not_1_out, not_2_out,
       not_3_out, not_4_out, not_5_out, not_6_out, not_7_out, not_8_out;

  Clock clock_1 (.out(clock_1_out));
  Button button_1 (.out(button_1_out));
  Clock clock_2 (.out(clock_2_out));
  Button button_2 (.out(button_2_out));
  Clock clock_3 (.out(clock_3_out));
  Button button_3 (.out(button_3_out));
  D_Flip_Flop d_ff_1 (.clk(clock_1_out), .D(in_1), .Q(out_13), .reset(button_1_out));  // open: Qn, preset, en
  S_R_Flip_Flop s_r_ff_1 (
    .S(in_5), .clk(clock_2_out), .R(not_1_out), .Q(out_17), .reset(button_2_out));  // open: Qn, preset, en
  not not_1 (not_1_out, in_5);
  not not_2 (not_2_out, in_9);
  J_K_Flip_Flop j_k_ff_1 (
    .J(in_9), .clk(clock_3_out), .K(not_2_out), .Q(out_21), .reset(button_3_out));  // open: Qn, preset, en
  D_Flip_Flop d_ff_2 (.clk(clock_1_out), .D(in_2), .Q(out_14), .reset(button_1_out));  // open: Qn, preset, en
  not not_3 (not_3_out, in_6);
  not not_4 (not_4_out, in_10);
  S_R_Flip_Flop s_r_ff_2 (
    .S(in_6), .clk(clock_2_out), .R(not_3_out), .Q(out_18), .reset(button_2_out));  // open: Qn, preset, en
  J_K_Flip_Flop j_k_ff_2 (
    .J(in_10), .clk(clock_3_out), .K(not_4_out), .Q(out_22), .reset(button_3_out));  // open: Qn, preset, en
  D_Flip_Flop d_ff_3 (.clk(clock_1_out), .D(in_3), .Q(out_15), .reset(button_1_out));  // open: Qn, preset, en
  S_R_Flip_Flop s_r_ff_3 (
    .S(in_7), .clk(clock_2_out), .R(not_5_out), .Q(out_19), .reset(button_2_out));  // open: Qn, preset, en
  not not_5 (not_5_out, in_7);
  not not_6 (not_6_out, in_11);
  J_K_Flip_Flop j_k_ff_3 (
    .J(in_11), .clk(clock_3_out), .K(not_6_out), .Q(out_23), .reset(button_3_out));  // open: Qn, preset, en
  D_Flip_Flop d_ff_4 (.clk(clock_1_out), .D(in_4), .Q(out_16), .reset(button_1_out));  // open: Qn, preset, en
  not not_7 (not_7_out, in_8);
  not not_8 (not_8_out, in_12);
  S_R_Flip_Flop s_r_ff_4 (
    .S(in_8), .clk(clock_2_out), .R(not_7_out), .Q(out_20), .reset(button_2_out));  // open: Qn, preset, en
  J_K_Flip_Flop j_k_ff_4 (
    .J(in_12), .clk(clock_3_out), .K(not_8_out), .Q(out_24), .reset(button_3_out));  // open: Qn, preset, en

  // Notes on the sheet:
  //   PIPO Using D flip Flop
  //   PIPO using SR flip flop
  //   PIPO using JK flip flop
endmodule
