// Logisim project PISO.circ as structural Verilog: 1 circuit, main circuit main
module main (
  input  in_1,
  input  in_2,
  input  in_3,
  input  in_4,
  input  in_5,
  input  in_6,
  input  in_7,
  input  in_8,
  input  in_9,
  input  in_10,
  output out_11,
  output out_12
);

  wire and_1_out, and_2_out, and_3_out, and_4_out, and_5_out, and_6_out, and_7_out, and_8_out, and_9_out,
       and_10_out, and_11_out, and_12_out, button_1_out, button_2_out, clock_1_out, clock_2_out, d_ff_1_q,
       d_ff_2_q, d_ff_3_q, not_1_out, not_2_out, not_3_out, not_4_out, not_5_out, not_6_out, or_1_out,
       or_2_out, or_3_out, or_4_out, or_5_out, or_6_out, s_r_ff_1_q, s_r_ff_2_q, s_r_ff_3_q;

  Clock clock_1 (.out(clock_1_out));
  Button button_1 (.out(button_1_out));
  Clock clock_2 (.out(clock_2_out));
  Button button_2 (.out(button_2_out));
  not not_1 (not_1_out, in_4);
  not not_2 (not_2_out, in_9);
  not not_3 (not_3_out, in_10);
  and and_1 (and_1_out, d_ff_1_q, in_4);
  D_Flip_Flop d_ff_1 (.clk(clock_1_out), .D(in_5), .Q(d_ff_1_q), .reset(button_1_out));  // open: Qn, preset, en
  S_R_Flip_Flop s_r_ff_1 (
    .S(in_10), .clk(clock_2_out), .R(not_3_out), .Q(s_r_ff_1_q), .reset(button_2_out));  // open: Qn, preset, en
  and and_2 (and_2_out, not_1_out, in_1);
  or or_1 (or_1_out, and_1_out, and_2_out);
  and and_3 (and_3_out, not_2_out, in_6);
  and and_4 (and_4_out, s_r_ff_1_q, in_9);
  or or_2 (or_2_out, and_4_out, and_3_out);
  not not_4 (not_4_out, or_2_out);
  D_Flip_Flop d_ff_2 (.clk(clock_1_out), .D(or_1_out), .Q(d_ff_2_q), .reset(button_1_out));  // open: Qn, preset, en
  S_R_Flip_Flop s_r_ff_2 (
    .S(or_2_out), .clk(clock_2_out), .R(not_4_out), .Q(s_r_ff_2_q), .reset(button_2_out));  // open: Qn, preset, en
  and and_5 (and_5_out, d_ff_2_q, in_4);
  or or_3 (or_3_out, and_5_out, and_7_out);
  and and_6 (and_6_out, s_r_ff_2_q, in_9);
  and and_7 (and_7_out, not_1_out, in_2);
  and and_8 (and_8_out, not_2_out, in_7);
  or or_4 (or_4_out, and_6_out, and_8_out);
  not not_5 (not_5_out, or_4_out);
  D_Flip_Flop d_ff_3 (.clk(clock_1_out), .D(or_3_out), .Q(d_ff_3_q), .reset(button_1_out));  // open: Qn, preset, en
  S_R_Flip_Flop s_r_ff_3 (
    .S(or_4_out), .clk(clock_2_out), .R(not_5_out), .Q(s_r_ff_3_q), .reset(button_2_out));  // open: Qn, preset, en
  and and_9 (and_9_out, d_ff_3_q, in_4);
  or or_5 (or_5_out, and_9_out, and_11_out);
  and and_10 (and_10_out, s_r_ff_3_q, in_9);
  or or_6 (or_6_out, and_10_out, and_12_out);
  and and_11 (and_11_out, not_1_out, in_3);
  and and_12 (and_12_out, not_2_out, in_8);
  not not_6 (not_6_out, or_6_out);
  D_Flip_Flop d_ff_4 (.clk(clock_1_out), .D(or_5_out), .Q(out_11), .reset(button_1_out));  // open: Qn, preset, en
  S_R_Flip_Flop s_r_ff_4 (
    .S(or_6_out), .clk(clock_2_out), .R(not_6_out), .Q(out_12), .reset(button_2_out));  // open: Qn, preset, en

  // Notes on the sheet:
  //   PISO using D flip Flop
  //   PISO using SR Flip Flop
endmodule
