// Logisim project RippleCarryAdder.circ as structural Verilog
// FullAdder
module FuLLAdder (
  input  A,
  input  B,
  input  C,
  output out_4,
  output out_5
);

  wire and_1_out, and_2_out, xor_1_out;

  xor xor_1 (xor_1_out, A, B);
  and and_1 (and_1_out, A, B);
  and and_2 (and_2_out, C, xor_1_out);
  xor xor_2 (out_4, xor_1_out, C);
  or or_1 (out_5, and_1_out, and_2_out);

  // Notes on the sheet:
  //   Full Adder
endmodule

module Half_Adder (
  input  B4,
  input  A4,
  input  B2,
  input  A2,
  input  B1,
  input  A1,
  input  B0,
  input  A0,
  input  C0,
  output c4,
  output S3,
  output S2,
  output S1,
  output S0
);

  wire fulladder_2_out_5, fulladder_3_out_5, fulladder_4_out_5;

  FuLLAdder fulladder_1 (.A(A4), .B(B4), .C(fulladder_2_out_5), .out_4(S3), .out_5(c4));
  FuLLAdder fulladder_2 (.A(A2), .B(B2), .C(fulladder_3_out_5), .out_4(S2), .out_5(fulladder_2_out_5));
  FuLLAdder fulladder_3 (.A(A1), .B(B1), .C(fulladder_4_out_5), .out_4(S1), .out_5(fulladder_3_out_5));
  FuLLAdder fulladder_4 (.A(A0), .B(B0), .C(C0), .out_4(S0), .out_5(fulladder_4_out_5));

  // Notes on the sheet:
  //   C3
  //   Ripple Carry Adder
  //   C2
  //   C1
endmodule
