// Logisim project SIPO.circ as structural Verilog: 1 circuit, main circuit main
module main (
  input  in_1,
  input  in_2,
  input  in_3,
  output out_4,
  output out_5,
  output out_6,
  output out_7,
  output out_8,
  output out_9,
  output out_10,
  output out_11,
  output out_12,
  output out_13,
  output out_14,
  output out_15
);

  wire button_1_out, button_2_out, button_3_out, clock_1_out, clock_2_out, clock_3_out, not_1_out, not_2_out,
       not_3_out, not_4_out, not_5_out, not_6_out, not_7_out, not_8_out;

  Clock clock_1 (.out(clock_1_out));
  Button button_1 (.out(button_1_out));
  Clock clock_2 (.out(clock_2_out));
  Button button_2 (.out(button_2_out));
  Clock clock_3 (.out(clock_3_out));
  Button button_3 (.out(button_3_out));
  not not_1 (not_1_out, in_2);
  not not_2 (not_2_out, in_3);
  D_Flip_Flop d_ff_1 (.clk(clock_1_out), .D(in_1), .Q(out_4), .reset(button_1_out));  // open: Qn, preset, en
  S_R_Flip_Flop s_r_ff_1 (
    .S(in_2), .clk(clock_2_out), .R(not_1_out), .Q(out_8), .reset(button_2_out));  // open: Qn, preset, en
  J_K_Flip_Flop j_k_ff_1 (
    .J(in_3), .clk(clock_3_out), .K(not_2_out), .Q(out_12), .reset(button_3_out));  // open: Qn, preset, en
  not not_3 (not_3_out, out_8);
  not not_4 (not_4_out, out_12);
  D_Flip_Flop d_ff_2 (.clk(clock_1_out), .D(out_4), .Q(out_5), .reset(button_1_out));  // open: Qn, preset, en
  S_R_Flip_Flop s_r_ff_2 (
    .S(out_8), .clk(clock_2_out), .R(not_3_out), .Q(out_9), .reset(button_2_out));  // open: Qn, preset, en
  J_K_Flip_Flop j_k_ff_2 (
    .J(out_12), .clk(clock_3_out), .K(not_4_out), .Q(out_13), .reset(button_3_out));  // open: Qn, preset, en
  not not_5 (not_5_out, out_9);
  not not_6 (not_6_out, out_13);
  D_Flip_Flop d_ff_3 (.clk(clock_1_out), .D(out_5), .Q(out_6), .reset(button_1_out));  // open: Qn, preset, en
  S_R_Flip_Flop s_r_ff_3 (
    .S(out_9), .clk(clock_2_out), .R(not_5_out), .Q(out_10), .reset(button_2_out));  // open: Qn, preset, en
  J_K_Flip_Flop j_k_ff_3 (
    .J(out_13), .clk(clock_3_out), .K(not_6_out), .Q(out_14), .reset(button_3_out));  // open: Qn, preset, en
  not not_7 (not_7_out, out_10);
  D_Flip_Flop d_ff_4 (.clk(clock_1_out), .D(out_6), .Q(out_7), .reset(button_1_out));  // open: Qn, preset, en
  S_R_Flip_Flop s_r_ff_4 (
    .S(out_10), .clk(clock_2_out), .R(not_7_out), .Q(out_11), .reset(button_2_out));  // open: Qn, preset, en
  J_K_Flip_Flop j_k_ff_4 (
    .J(out_14), .clk(clock_3_out), .K(not_8_out), .Q(out_15), .reset(button_3_out));  // open: Qn, preset, en
  not not_8 (not_8_out, out_14);

  // Notes on the sheet:
  //   SIPO using D flip flop
  //   SIPO using SR flip flop
  //   SIPO using JK flip flop
endmodule
