// Logisim project SISO.circ as structural Verilog: 1 circuit, main circuit main
module main (
  input  in_1,
  input  in_2,
  input  in_3,
  output out_4,
  output out_5,
  output out_6
);

  wire button_1_out, button_2_out, button_3_out, clock_1_out, clock_2_out, clock_3_out, d_ff_1_q, d_ff_2_q,
       d_ff_3_q, j_k_ff_1_q, j_k_ff_2_q, j_k_ff_3_q, not_1_out, not_2_out, not_3_out, not_4_out, not_5_out,
       not_6_out, not_7_out, not_8_out, s_r_ff_1_q, s_r_ff_2_q, s_r_ff_3_q;

  Clock clock_1 (.out(clock_1_out));
  Button button_1 (.out(button_1_out));
  Clock clock_2 (.out(clock_2_out));
  Button button_2 (.out(button_2_out));
  Clock clock_3 (.out(clock_3_out));
  Button button_3 (.out(button_3_out));
  not not_1 (not_1_out, in_2);
  not not_2 (not_2_out, in_3);
  D_Flip_Flop d_ff_1 (.clk(clock_1_out), .D(in_1), .Q(d_ff_1_q), .reset(button_1_out));  // open: Qn, preset, en
  S_R_Flip_Flop s_r_ff_1 (
    .S(in_2), .clk(clock_2_out), .R(not_1_out), .Q(s_r_ff_1_q), .reset(button_2_out));  // open: Qn, preset, en
  J_K_Flip_Flop j_k_ff_1 (
    .J(in_3), .clk(clock_3_out), .K(not_2_out), .Q(j_k_ff_1_q), .reset(button_3_out));  // open: Qn, preset, en
  D_Flip_Flop d_ff_2 (.clk(clock_1_out), .D(d_ff_1_q), .Q(d_ff_2_q), .reset(button_1_out));  // open: Qn, preset, en
  not not_3 (not_3_out, s_r_ff_1_q);
  not not_4 (not_4_out, j_k_ff_1_q);
  S_R_Flip_Flop s_r_ff_2 (
    .S(s_r_ff_1_q), .clk(clock_2_out), .R(not_3_out), .Q(s_r_ff_2_q), .reset(button_2_out));  // open: Qn, preset, en
  not not_5 (not_5_out, s_r_ff_2_q);
  J_K_Flip_Flop j_k_ff_2 (
    .J(j_k_ff_1_q), .clk(clock_3_out), .K(not_4_out), .Q(j_k_ff_2_q), .reset(button_3_out));  // open: Qn, preset, en
  not not_6 (not_6_out, j_k_ff_2_q);
  D_Flip_Flop d_ff_3 (.clk(clock_1_out), .D(d_ff_2_q), .Q(d_ff_3_q), .reset(button_1_out));  // open: Qn, preset, en
  S_R_Flip_Flop s_r_ff_3 (
    .S(s_r_ff_2_q), .clk(clock_2_out), .R(not_5_out), .Q(s_r_ff_3_q), .reset(button_2_out));  // open: Qn, preset, en
  J_K_Flip_Flop j_k_ff_3 (
    .J(j_k_ff_2_q), .clk(clock_3_out), .K(not_6_out), .Q(j_k_ff_3_q), .reset(button_3_out));  // open: Qn, preset, en
  not not_7 (not_7_out, s_r_ff_3_q);
  not not_8 (not_8_out, j_k_ff_3_q);
  D_Flip_Flop d_ff_4 (.clk(clock_1_out), .D(d_ff_3_q), .Q(out_4), .reset(button_1_out));  // open: Qn, preset, en
  S_R_Flip_Flop s_r_ff_4 (
    .S(s_r_ff_3_q), .clk(clock_2_out), .R(not_7_out), .Q(out_5), .reset(button_2_out));  // open: Qn, preset, en
  J_K_Flip_Flop j_k_ff_4 (
    .J(j_k_ff_3_q), .clk(clock_3_out), .K(not_8_out), .Q(out_6), .reset(button_3_out));  // open: Qn, preset, en

  // Notes on the sheet:
  //   SISO Using D Flip Flop
  //   SISO Using SR flip flop
  //   SISO Using JK flip flop
endmodule
