// Logisim project SR flipflop.circ as structural Verilog: 1 circuit, main circuit main
module main (
  input  IN
);

  wire clock_1_out, not_1_out, s_r_ff_1_q, s_r_ff_1_qn, s_r_ff_2_q, s_r_ff_2_qn, s_r_ff_3_q, s_r_ff_3_qn,
       s_r_ff_4_q;

  Clock clock_1 (.out(clock_1_out));
  not not_1 (not_1_out, IN);
  S_R_Flip_Flop s_r_ff_1 (
    .S(IN), .clk(clock_1_out), .R(not_1_out), .Q(s_r_ff_1_q), .Qn(s_r_ff_1_qn));  // open: preset, reset, en
  LED led_1 (.in(s_r_ff_1_q));
  S_R_Flip_Flop s_r_ff_2 (
    .S(s_r_ff_1_q), .clk(clock_1_out), .R(s_r_ff_1_qn), .Q(s_r_ff_2_q), .Qn(s_r_ff_2_qn));  // open: preset, reset, en
  LED led_2 (.in(s_r_ff_2_q));
  S_R_Flip_Flop s_r_ff_3 (
    .S(s_r_ff_2_q), .clk(clock_1_out), .R(s_r_ff_2_qn), .Q(s_r_ff_3_q), .Qn(s_r_ff_3_qn));  // open: preset, reset, en
  LED led_3 (.in(s_r_ff_3_q));
  S_R_Flip_Flop s_r_ff_4 (
    .S(s_r_ff_3_q), .clk(clock_1_out), .R(s_r_ff_3_qn), .Q(s_r_ff_4_q));  // open: Qn, preset, reset, en
  LED led_4 (.in(s_r_ff_4_q));

  // Notes on the sheet:
  //   CLK
  //   Q1
  //   SR- Flip-Flop
  //   Q2
  //   Q3
  //   Q4
endmodule
