// Logisim project Shift T=Register.circ as structural Verilog: 5 circuits, main circuit main
module main (
  input  in_1,
  input  in_2,
  input  in_3,
  input  in_4,
  input  in_5,
  input  in_6,
  input  in_7,
  input  in_8,
  input  in_9,
  output out_10,
  output out_11,
  output out_12,
  output out_13
);

  wire mux_1_output, mux_2_output, mux_3_output, mux_4_output;

  D_Flip_Flop d_flip_flop_1 (.D(mux_1_output), .E(in_1), .Q(out_10));  // open: Q_prime
  Mux mux_1 (.S1(in_2), .S2(in_3), .I1(in_4), .I2(out_11), .I3(in_8), .I4(out_10), .Output(mux_1_output));
  D_Flip_Flop d_flip_flop_2 (.D(mux_2_output), .E(in_1), .Q(out_11));  // open: Q_prime
  Mux mux_2 (.S1(in_2), .S2(in_3), .I1(in_5), .I2(out_12), .I3(out_10), .I4(out_11), .Output(mux_2_output));
  D_Flip_Flop d_flip_flop_3 (.D(mux_3_output), .E(in_1), .Q(out_12));  // open: Q_prime
  Mux mux_3 (.S1(in_2), .S2(in_3), .I1(in_6), .I2(out_13), .I3(out_11), .I4(out_12), .Output(mux_3_output));
  D_Flip_Flop d_flip_flop_4 (.D(mux_4_output), .E(in_1), .Q(out_13));  // open: Q_prime
  Mux mux_4 (.S1(in_2), .S2(in_3), .I1(in_7), .I2(in_9), .I3(out_12), .I4(out_13), .Output(mux_4_output));
endmodule

module D_Flip_Flop (
  input  D,
  input  E,
  output Q,
  output Q_prime
);

  wire nand_1_out, nand_2_out, not_1_out;

  not not_1 (not_1_out, D);
  nand nand_1 (nand_1_out, D, E);
  nand nand_2 (nand_2_out, E, not_1_out);
  nand nand_3 (Q, nand_1_out, Q_prime);
  nand nand_4 (Q_prime, Q, nand_2_out);
endmodule

module Mux (
  input  S1,
  input  S2,
  input  I1,
  input  I2,
  input  I3,
  input  I4,
  output Output
);

  wire and_1_out, and_2_out, and_3_out, and_4_out, not_1_out, not_2_out;

  not not_1 (not_1_out, S1);
  not not_2 (not_2_out, S2);
  and and_1 (and_1_out, S1, S2, I1);
  and and_2 (and_2_out, S1, not_2_out, I2);
  and and_3 (and_3_out, not_1_out, S2, I3);
  and and_4 (and_4_out, not_2_out, not_1_out, I4);
  or or_1 (Output, and_1_out, and_2_out, and_3_out, and_4_out);
endmodule

module Shift_Resgister (
  input  in_1,
  input  [1:0] in_2,
  input  in_3,
  input  in_4,
  input  in_5,
  input  in_6,
  input  in_7,
  input  in_8,
  output out_9,
  output out_10,
  output out_11,
  output out_12
);

  wire clock_1_out, multiplexer_1_out, multiplexer_2_out, multiplexer_3_out, multiplexer_4_out;

  Clock clock_1 (.out(clock_1_out));
  Multiplexer #(.select(2), .enable("false")) multiplexer_1 (
    .in0(in_5), .in1(out_10), .in2(in_3), .in3(out_9), .out(multiplexer_1_out), .sel(in_2));
  D_Flip_Flop_part d_ff_1 (.clk(clock_1_out), .D(multiplexer_1_out), .Q(out_9), .en(in_1));  // open: Qn, preset, reset
  D_Flip_Flop_part d_ff_2 (.clk(clock_1_out), .D(multiplexer_2_out), .Q(out_10), .en(in_1));  // open: Qn, preset, reset
  Multiplexer #(.select(2), .enable("false")) multiplexer_2 (
    .in0(in_6), .in1(out_11), .in2(out_9), .in3(out_10), .out(multiplexer_2_out), .sel(in_2));
  Multiplexer #(.select(2), .enable("false")) multiplexer_3 (
    .in0(in_7), .in1(out_12), .in2(out_10), .in3(out_11), .out(multiplexer_3_out), .sel(in_2));
  D_Flip_Flop_part d_ff_3 (.clk(clock_1_out), .D(multiplexer_3_out), .Q(out_11), .en(in_1));  // open: Qn, preset, reset
  D_Flip_Flop_part d_ff_4 (.clk(clock_1_out), .D(multiplexer_4_out), .Q(out_12), .en(in_1));  // open: Qn, preset, reset
  Multiplexer #(.select(2), .enable("false")) multiplexer_4 (
    .in0(in_8), .in1(in_4), .in2(out_11), .in3(out_12), .out(multiplexer_4_out), .sel(in_2));
endmodule

module _1 (
);

  D_Flip_Flop d_flip_flop_1 ();  // open: D, E, Q, Q_prime
endmodule
