// Logisim project ShiftRegister.circ as structural Verilog: 1 circuit, main circuit main
module main (
  input  Shift_right,
  input  I4,
  input  I3,
  input  I2,
  input  Shift_left,
  input  I1,
  input  [1:0] Select_Bits,
  output A1,
  output A2,
  output A3,
  output A4
);

  wire Clear_out, Clock_out, multiplexer_1_out, multiplexer_2_out, multiplexer_3_out, multiplexer_4_out;

  Multiplexer #(.select(2)) multiplexer_1 (
    .in0(A1), .in1(Shift_right), .in2(A2), .in3(I4), .out(multiplexer_1_out), .sel(Select_Bits));  // open: en
  Multiplexer #(.select(2)) multiplexer_2 (
    .in0(A2), .in1(A1), .in2(A3), .in3(I3), .out(multiplexer_2_out), .sel(Select_Bits));  // open: en
  Multiplexer #(.select(2)) multiplexer_3 (
    .in0(A3), .in1(A2), .in2(A4), .in3(I2), .out(multiplexer_3_out), .sel(Select_Bits));  // open: en
  Multiplexer #(.select(2)) multiplexer_4 (
    .in0(A4), .in1(A3), .in2(Shift_left), .in3(I1), .out(multiplexer_4_out), .sel(Select_Bits));  // open: en
  Clock Clock (.out(Clock_out));
  D_Flip_Flop d_ff_1 (.clk(Clock_out), .D(multiplexer_1_out), .Q(A1), .reset(Clear_out));  // open: Qn, preset, en
  D_Flip_Flop d_ff_2 (.clk(Clock_out), .D(multiplexer_2_out), .Q(A2), .reset(Clear_out));  // open: Qn, preset, en
  D_Flip_Flop d_ff_3 (.clk(Clock_out), .D(multiplexer_3_out), .Q(A3), .reset(Clear_out));  // open: Qn, preset, en
  D_Flip_Flop d_ff_4 (.clk(Clock_out), .D(multiplexer_4_out), .Q(A4), .reset(Clear_out));  // open: Qn, preset, en
  Button Clear (.out(Clear_out));
endmodule
