// Logisim project T using JK.circ as structural Verilog: 1 circuit, main circuit main
module main (
  input  in_1,
  input  in_2,
  output out_3,
  output out_4,
  output out_5,
  output out_6
);

  wire clock_1_out, clock_2_out, nand_1_out, nand_2_out;

  Clock clock_1 (.out(clock_1_out));
  nand nand_1 (nand_1_out, out_4, in_1, clock_1_out);
  nand nand_2 (nand_2_out, clock_1_out, in_1, out_3);
  Clock clock_2 (.out(clock_2_out));
  J_K_Flip_Flop j_k_ff_1 (.J(in_2), .clk(clock_2_out), .K(in_2), .Q(out_5), .Qn(out_6));  // open: preset, en, reset
  nand nand_3 (out_3, nand_1_out, out_4);
  nand nand_4 (out_4, out_3, nand_2_out);
endmodule
