// Logisim project odd_even_parity_checker.circ as structural Verilog: 1 circuit, main circuit main
module main (
  input  A,
  input  B,
  input  C,
  input  P,
  input  A_2,
  input  B_2,
  input  C_2,
  input  P_2,
  output out_9,
  output out_10
);

  ExactlyOne xor_1 (.out(out_9), .in0(A), .in1(B), .in2(C), .in3(P));
  NotExactlyOne xnor_1 (.out(out_10), .in0(A_2), .in1(B_2), .in2(C_2), .in3(P_2));

  // Notes on the sheet:
  //   Even Parity Checker
  //   Odd Parity Checker
endmodule
